// Digital circuit D_LatchEnable_SetClear.dig as structural Verilog
module D_LatchEnable_SetClear (
  input  D,
  input  Enable,
  input  Set,
  input  Clear,
  output Q
);

  wire nand_1_out, nand_2_out, nand_4_out, not_1_out;

  not not_1 (not_1_out, D);
  nand nand_1 (nand_1_out, D, Enable);
  nand nand_2 (nand_2_out, Enable, not_1_out);
  nand nand_3 (Q, Set, nand_1_out, nand_4_out);
  nand nand_4 (nand_4_out, Q, nand_2_out, Clear);

  // Notes on the sheet:
  //   Set: default 1
  //   Clear: default 1
endmodule
