// Digital circuit Register.dig as structural Verilog
module Register (
  input  Enable,
  input  Clock,
  input  Clear,
  input  Set,
  input  D3,
  input  D2,
  input  D1,
  input  D0,
  output out_9,
  output out_10,
  output out_11,
  output out_12
);

  wire multiplexer_1_out, multiplexer_2_out, multiplexer_3_out, multiplexer_4_out;

  Multiplexer multiplexer_1 (.sel(Enable), .in_0(out_9), .in_1(D3), .out(multiplexer_1_out));
  D_FF_AS d_ff_as_1 (.Set(Set), .D(multiplexer_1_out), .C(Clock), .Clr(Clear), .Q(out_9));  // open: nQ
  Multiplexer multiplexer_2 (.sel(Enable), .in_0(out_10), .in_1(D2), .out(multiplexer_2_out));
  D_FF_AS d_ff_as_2 (.Set(Set), .D(multiplexer_2_out), .C(Clock), .Clr(Clear), .Q(out_10));  // open: nQ
  Multiplexer multiplexer_3 (.sel(Enable), .in_0(out_11), .in_1(D1), .out(multiplexer_3_out));
  D_FF_AS d_ff_as_3 (.Set(Set), .D(multiplexer_3_out), .C(Clock), .Clr(Clear), .Q(out_11));  // open: nQ
  Multiplexer multiplexer_4 (.sel(Enable), .in_0(out_12), .in_1(D0), .out(multiplexer_4_out));
  D_FF_AS d_ff_as_4 (.Set(Set), .D(multiplexer_4_out), .C(Clock), .Clr(Clear), .Q(out_12));  // open: nQ
endmodule
