// Digital circuit 4_Input_Or_Madeof_NAND.dig as structural Verilog
module _4_Input_Or_Madeof_NAND (
  input  A,
  input  B,
  input  C,
  input  D,
  output Out
);

  wire nand_1_out, nand_2_out, nand_3_out, nand_4_out, nand_5_out, nand_6_out;

  nand nand_1 (nand_1_out, A, A, A);
  nand nand_2 (nand_2_out, B, B, B);
  nand nand_3 (nand_3_out, C, C, C);
  nand nand_4 (nand_4_out, D, D, D);
  nand nand_5 (nand_5_out, nand_1_out, nand_2_out, nand_3_out);
  nand nand_6 (nand_6_out, nand_5_out, nand_5_out, nand_5_out);
  nand nand_7 (Out, nand_6_out, nand_6_out, nand_4_out);

  // Notes on the sheet:
  //   A¬
  //   B¬
  //   C¬
  //   D¬
  //   ABC
  //   ABC¬
  //   A+B+C+D
endmodule
