// Digital circuit Ejercicio_3_Solucion_NAND.dig as structural Verilog
module Ejercicio_3_Solucion_NAND (
  input  x,
  input  y,
  input  z,
  output f
);

  wire nand_1_out, nand_2_out, nand_3_out, nand_4_out, nand_5_out, nand_6_out, nand_7_out, nand_8_out;

  nand nand_1 (nand_1_out, x, x, x);
  nand nand_2 (nand_2_out, y, y, y);
  nand nand_3 (nand_3_out, z, nand_2_out, nand_1_out);
  nand nand_4 (nand_4_out, z, y, nand_1_out);
  nand nand_5 (nand_5_out, z, nand_2_out, x);
  nand nand_6 (nand_6_out, y, x, x);
  nand nand_7 (nand_7_out, nand_3_out, nand_4_out, nand_5_out);
  nand nand_8 (nand_8_out, nand_7_out, nand_7_out, nand_7_out);
  nand nand_9 (f, nand_8_out, nand_8_out, nand_6_out);

  // Notes on the sheet:
  //   x¬y¬z
  //   x¬yz
  //   xy¬z
  //   xy
  //   A¬
  //   B¬
  //   C¬
  //   D¬
  //   ABC
  //   ABC¬
  //   A+B+C+D
endmodule
