// Digital circuit Ejercicios_motores.dig as structural Verilog
module Ejercicios_motores (
  input  _5_KW,
  input  _10_KW,
  input  _15_KW,
  output G1,
  output G2
);

  wire or_2_out;

  or or_1 (G1, _5_KW, _10_KW, _15_KW);
  or or_2 (or_2_out, _5_KW, _10_KW);
  and and_1 (G2, or_2_out, _15_KW);
endmodule
