// Digital circuit XOR_Madeof_NAND.dig as structural Verilog
module XOR_Madeof_NAND (
  input  A,
  input  B,
  output Out
);

  wire nand_1_out, nand_2_out, nand_3_out;

  nand nand_1 (nand_1_out, A, B);
  nand nand_2 (nand_2_out, A, nand_1_out);
  nand nand_3 (nand_3_out, nand_1_out, B);
  nand nand_4 (Out, nand_2_out, nand_3_out);

  // Notes on the sheet:
  //   A¬B¬
  //   (A(A¬B¬))¬
  //   AB¬+A¬B
endmodule
