// Digital circuit ej3.dig as structural Verilog
module ej3 (
  input  A,
  input  B,
  output Output
);

  wire nfet_1_s, nfet_3_s, Output_1;

  PFET pfet_1 (.G(A), .S(1'b1), .D(Output_1));
  NFET nfet_1 (.G(B), .D(Output_1), .S(nfet_1_s));
  NFET nfet_2 (.G(A), .D(nfet_1_s), .S(1'b0));
  PFET pfet_2 (.G(B), .S(1'b1), .D(Output_1));
  PFET pfet_3 (.G(Output_1), .S(1'b1), .D(Output));
  NFET nfet_3 (.G(Output_1), .D(Output), .S(nfet_3_s));
  NFET nfet_4 (.G(Output_1), .D(nfet_3_s), .S(1'b0));
  PFET pfet_4 (.G(Output_1), .S(1'b1), .D(Output));

  // Other names for the same wires on the sheet: Input_A = A; Input_B = B
endmodule
