// Digital circuit ejemplo.dig as structural Verilog
module ejemplo (
  input  in_2,
  output out_1
);

  FGPFET fgpfet_1 (.G(in_2), .S(1'b1), .D(out_1));
  FGNFET fgnfet_1 (.G(in_2), .D(out_1), .S(1'b0));
endmodule
