// Digital circuit Prueba_GPIO_1bit.dig as structural Verilog
module Prueba_GPIO_1bit (
  input  D,
  input  En,
  input  C,
  input  S,
  input  D_2,
  input  C_2,
  input  S_2,
  input  In,
  input  C_3,
  input  S_3,
  input  Clock,
  output out_11
);

  wire d_ff_as_2_q, d_ff_as_3_q, driver_1_out, driverinvsel_1_out, multiplexer_1_out, multiplexer_2_out,
       multiplexer_3_out;

  Multiplexer multiplexer_1 (.sel(En), .in_0(out_11), .in_1(driverinvsel_1_out), .out(multiplexer_1_out));
  D_FF_AS d_ff_as_1 (.Set(S_3), .D(multiplexer_1_out), .C(Clock), .Clr(C_3), .Q(out_11));  // open: nQ
  Multiplexer multiplexer_2 (.sel(En), .in_0(d_ff_as_2_q), .in_1(D), .out(multiplexer_2_out));
  assign driverinvsel_1_out = ~d_ff_as_2_q ? In : 1'bz;  // DriverInvSel driverinvsel_1
  D_FF_AS d_ff_as_2 (.Set(S), .D(multiplexer_2_out), .C(Clock), .Clr(C), .Q(d_ff_as_2_q));  // open: nQ
  assign driver_1_out = d_ff_as_2_q ? d_ff_as_3_q : 1'bz;  // Driver driver_1
  LED Out (.in(driver_1_out));
  Multiplexer multiplexer_3 (.sel(En), .in_0(d_ff_as_3_q), .in_1(D_2), .out(multiplexer_3_out));
  D_FF_AS d_ff_as_3 (.Set(S_2), .D(multiplexer_3_out), .C(Clock), .Clr(C_2), .Q(d_ff_as_3_q));  // open: nQ

  // Other names for the same wires on the sheet: Clk = Clock; Enable = En

  // Notes on the sheet:
  //   Entrada
  //   Control (0 = Entrada , 1 = Salida )
  //   Salida
endmodule
