// Digital circuit Ex1_8to1_MUX.dig as structural Verilog
module Ex1_8to1_MUX (
  input  D_0,
  input  D_1,
  input  D_2,
  input  D_3,
  input  Sel_2,
  input  Sel_1,
  input  Sel_0,
  input  D_4,
  input  D_5,
  input  D_6,
  input  D_7,
  output Output
);

  wire and_1_out, and_2_out, and_3_out, and_4_out, and_5_out, and_6_out, and_7_out, and_8_out, not_1_out,
       not_2_out, not_3_out, or_1_out, or_2_out;

  not not_1 (not_1_out, Sel_2);
  not not_2 (not_2_out, Sel_1);
  not not_3 (not_3_out, Sel_0);
  and and_1 (and_1_out, D_0, not_3_out, not_2_out, not_1_out);
  and and_2 (and_2_out, D_1, Sel_0, not_2_out, not_1_out);
  and and_3 (and_3_out, D_2, not_3_out, Sel_1, not_1_out);
  and and_4 (and_4_out, D_3, Sel_0, Sel_1, not_1_out);
  and and_5 (and_5_out, D_4, not_3_out, not_2_out, Sel_2);
  and and_6 (and_6_out, D_5, Sel_0, not_2_out, Sel_2);
  and and_7 (and_7_out, D_6, not_3_out, Sel_1, Sel_2);
  and and_8 (and_8_out, D_7, Sel_0, Sel_1, Sel_2);
  or or_1 (or_1_out, and_1_out, and_2_out, and_3_out, and_4_out);
  or or_2 (or_2_out, and_5_out, and_6_out, and_7_out, and_8_out);
  or or_3 (Output, or_1_out, or_2_out);
endmodule
