// Digital circuit Ex2_1to4_DEMUX.dig as structural Verilog
module Ex2_1to4_DEMUX (
  input  S_1,
  input  D,
  input  S_0,
  output D_0,
  output D_1,
  output D_2,
  output D_3
);

  wire not_1_out, not_2_out;

  not not_1 (not_1_out, S_1);
  not not_2 (not_2_out, S_0);
  and and_1 (D_0, D, not_1_out, not_2_out);
  and and_2 (D_1, D, S_0, not_1_out);
  and and_3 (D_2, D, S_1, not_2_out);
  and and_4 (D_3, D, S_0, S_1);
endmodule
