// Digital circuit Ex3a_SR_FlipFlop.dig as structural Verilog
module Ex3a_SR_FlipFlop (
  input  S,
  input  R,
  input  Clock,
  output Q,
  output Q_2
);

  wire nand_1_out, nand_2_out, nand_3_out, nand_4_out, nand_5_out, nand_6_out, not_1_out;

  nand nand_1 (nand_1_out, S, Clock);
  nand nand_2 (nand_2_out, Clock, R);
  not not_1 (not_1_out, Clock);
  nand nand_3 (nand_3_out, nand_1_out, nand_4_out);
  nand nand_4 (nand_4_out, nand_3_out, nand_2_out);
  nand nand_5 (nand_5_out, nand_3_out, not_1_out);
  nand nand_6 (nand_6_out, not_1_out, nand_4_out);
  nand nand_7 (Q, nand_5_out, Q_2);
  nand nand_8 (Q_2, Q, nand_6_out);

  // Notes on the sheet:
  //   Master
  //   Un Flip Flop RS es un tipo de circuito secuencial que se usa para guardar un bit de informacion, se construye 
  //   usando dos SR Latch, donde uno actua como Master y el otro como Esclavo.
  //   Cuando se activa el Set de la entrada del Master, y el Clock esta en un flanco de subida (0->1), su salida Q 
  //   cambia a 1; sin embargo, el estado del Slave permanece sin cambios, para que el cambio en el Master se aplique
  //    en el Slave la señal del Clock debe estar en un flanco de bajada (1->0). Haciendo asi, que la salida Q del Slave sea 
  //   igual a la misma salida del Master. El estado del Slave permanece hasta que haya un cambio en el Master y 
  //   tambien en la señal del Clock.
  //   En este tipo de Flip Flop, no se pueden tener activos el Set y el Reset, ya que al estar los dos generan un estado de 
  //   oscilacion o tambien conocido como "Race condition".
  //   S'
  //   R'
  //   SR Latch
  //   Slave
endmodule
