// Digital circuit Ex3b_JK_FlipFlop.dig as structural Verilog
module Ex3b_JK_FlipFlop (
  input  J,
  input  K,
  input  Clock,
  output Q,
  output Q_2
);

  wire and_1_out, and_2_out, nand_1_out, nand_2_out, nand_3_out, nand_4_out, nand_5_out, nand_6_out,
       not_1_out;

  and and_1 (and_1_out, Q_2, J);
  and and_2 (and_2_out, K, Q);
  nand nand_1 (nand_1_out, and_1_out, Clock);
  nand nand_2 (nand_2_out, Clock, and_2_out);
  not not_1 (not_1_out, Clock);
  nand nand_3 (nand_3_out, nand_1_out, nand_4_out);
  nand nand_4 (nand_4_out, nand_3_out, nand_2_out);
  nand nand_5 (nand_5_out, nand_3_out, not_1_out);
  nand nand_6 (nand_6_out, not_1_out, nand_4_out);
  nand nand_7 (Q, nand_5_out, Q_2);
  nand nand_8 (Q_2, Q, nand_6_out);

  // Notes on the sheet:
  //   Master
  //   El funcionamiento del JK es secuencial y es exactamente el mismo al del SR. La principal diferencia entre 
  //   un flip flop RS y un JK, es la manera en que responden al tener ambas entradas en 1, en el caso del RS, 
  //   se produce un estado indefinido que no es aprovechable, mientras que en el JK se evita este estado, 
  //   y se reemplaza por estado controlado de alternancia (Toggling). El cual se logra, con la adicion de 
  //   dos compuertas AND que reciben como entradas los pares JQ' y KQ, estas compuertas se conectan a las
  //   entradas S y R respectivamente.
  //   S'
  //   R'
  //   SR Latch
  //   Slave
endmodule
