// Digital circuit Ex4_4pin_GPIO.dig as structural Verilog
module Ex4_4pin_GPIO (
  input  Enable_Control,
  input  Clear,
  input  Set,
  input  D4,
  input  D3,
  input  D2,
  input  D1,
  input  Clock,
  input  In_1,
  input  In_2,
  input  In_3,
  input  In_4,
  input  Pin_1,
  input  Pin_2,
  input  Pin_3,
  input  Pin_4,
  input  Enable_In,
  input  Enable_Out,
  output D_4,
  output D_3,
  output D_2,
  output D_1,
  output Out_1,
  output Out_2,
  output Out_3,
  output Out_4
);

  wire d_ff_as_4_q, d_ff_as_6_q, d_ff_as_7_q, d_ff_as_8_q, multiplexer_1_out, multiplexer_2_out,
       multiplexer_3_out, multiplexer_4_out, multiplexer_5_out, multiplexer_6_out, multiplexer_7_out,
       multiplexer_8_out, multiplexer_9_out, multiplexer_10_out, multiplexer_11_out, multiplexer_12_out,
       R_In1, R_In2, R_In3, R_In4, R_Out1, R_Out2, R_Out3, R_Out4;

  PullDown pulldown_1 (.out(R_In4));
  Multiplexer multiplexer_1 (.sel(Enable_In), .in_0(D_4), .in_1(R_In4), .out(multiplexer_1_out));
  D_FF_AS d_ff_as_1 (.Set(Set), .D(multiplexer_1_out), .C(Clock), .Clr(Clear), .Q(D_4));  // open: nQ
  PullDown pulldown_2 (.out(R_In3));
  Multiplexer multiplexer_2 (.sel(Enable_In), .in_0(D_3), .in_1(R_In3), .out(multiplexer_2_out));
  D_FF_AS d_ff_as_2 (.Set(Set), .D(multiplexer_2_out), .C(Clock), .Clr(Clear), .Q(D_3));  // open: nQ
  PullDown pulldown_3 (.out(R_In2));
  Multiplexer multiplexer_3 (.sel(Enable_In), .in_0(D_2), .in_1(R_In2), .out(multiplexer_3_out));
  D_FF_AS d_ff_as_3 (.Set(Set), .D(multiplexer_3_out), .C(Clock), .Clr(Clear), .Q(D_2));  // open: nQ
  Multiplexer multiplexer_4 (.sel(Enable_Control), .in_0(d_ff_as_4_q), .in_1(Pin_4), .out(multiplexer_4_out));
  PullDown pulldown_4 (.out(R_In1));
  Multiplexer multiplexer_5 (.sel(Enable_In), .in_0(D_1), .in_1(R_In1), .out(multiplexer_5_out));
  D_FF_AS d_ff_as_4 (.Set(Set), .D(multiplexer_4_out), .C(Clock), .Clr(Clear), .Q(d_ff_as_4_q));  // open: nQ
  assign R_In4 = ~d_ff_as_4_q ? In_4 : 1'bz;  // DriverInvSel driverinvsel_1
  D_FF_AS d_ff_as_5 (.Set(Set), .D(multiplexer_5_out), .C(Clock), .Clr(Clear), .Q(D_1));  // open: nQ
  Multiplexer multiplexer_6 (.sel(Enable_Control), .in_0(d_ff_as_6_q), .in_1(Pin_3), .out(multiplexer_6_out));
  assign Out_4 = d_ff_as_4_q ? R_Out4 : 1'bz;  // Driver driver_1
  D_FF_AS d_ff_as_6 (.Set(Set), .D(multiplexer_6_out), .C(Clock), .Clr(Clear), .Q(d_ff_as_6_q));  // open: nQ
  assign R_In3 = ~d_ff_as_6_q ? In_3 : 1'bz;  // DriverInvSel driverinvsel_2
  Multiplexer multiplexer_7 (.sel(Enable_Control), .in_0(d_ff_as_7_q), .in_1(Pin_2), .out(multiplexer_7_out));
  assign Out_3 = d_ff_as_6_q ? R_Out3 : 1'bz;  // Driver driver_2
  D_FF_AS d_ff_as_7 (.Set(Set), .D(multiplexer_7_out), .C(Clock), .Clr(Clear), .Q(d_ff_as_7_q));  // open: nQ
  assign R_In2 = ~d_ff_as_7_q ? In_2 : 1'bz;  // DriverInvSel driverinvsel_3
  Multiplexer multiplexer_8 (.sel(Enable_Control), .in_0(d_ff_as_8_q), .in_1(Pin_1), .out(multiplexer_8_out));
  assign Out_2 = d_ff_as_7_q ? R_Out2 : 1'bz;  // Driver driver_3
  Multiplexer multiplexer_9 (.sel(Enable_Out), .in_0(R_Out4), .in_1(D4), .out(multiplexer_9_out));
  D_FF_AS d_ff_as_8 (.Set(Set), .D(multiplexer_8_out), .C(Clock), .Clr(Clear), .Q(d_ff_as_8_q));  // open: nQ
  assign R_In1 = ~d_ff_as_8_q ? In_1 : 1'bz;  // DriverInvSel driverinvsel_4
  assign Out_1 = d_ff_as_8_q ? R_Out1 : 1'bz;  // Driver driver_4
  D_FF_AS d_ff_as_9 (.Set(Set), .D(multiplexer_9_out), .C(Clock), .Clr(Clear), .Q(R_Out4));  // open: nQ
  Multiplexer multiplexer_10 (.sel(Enable_Out), .in_0(R_Out3), .in_1(D3), .out(multiplexer_10_out));
  D_FF_AS d_ff_as_10 (.Set(Set), .D(multiplexer_10_out), .C(Clock), .Clr(Clear), .Q(R_Out3));  // open: nQ
  Multiplexer multiplexer_11 (.sel(Enable_Out), .in_0(R_Out2), .in_1(D2), .out(multiplexer_11_out));
  D_FF_AS d_ff_as_11 (.Set(Set), .D(multiplexer_11_out), .C(Clock), .Clr(Clear), .Q(R_Out2));  // open: nQ
  Multiplexer multiplexer_12 (.sel(Enable_Out), .in_0(R_Out1), .in_1(D1), .out(multiplexer_12_out));
  D_FF_AS d_ff_as_12 (.Set(Set), .D(multiplexer_12_out), .C(Clock), .Clr(Clear), .Q(R_Out1));  // open: nQ

  // Other names for the same wires on the sheet: En_Ctrl = Enable_Control; En_In = Enable_In; En_Out = Enable_Out

  // Notes on the sheet:
  //   Clock: Hz: 10
  //   Registro de entrada
  //   Registro de configuracion
  //   Pines/Entradas/Salidas
  //   Pin_i = 0 => Entrada
  //   Pin_i = 1 => Salida
  //   Registro de salida
endmodule
