// Digital circuit Counter_Register_BCD_7Segments.dig as structural Verilog
module Counter_Register_BCD_7Segments (
  input  Enable,
  input  Clock,
  input  Clear,
  input  Counter,
  input  Set,
  output Overflow
);

  wire a, and_2_out, and_3_out, and_4_out, and_5_out, and_6_out, and_7_out, and_8_out, and_9_out, and_10_out,
       and_11_out, and_12_out, and_13_out, and_14_out, b, c, d, d_ff_as_1_q, d_ff_as_2_q, d_ff_as_3_q,
       d_ff_as_4_q, e, f, g, multiplexer_1_out, multiplexer_2_out, multiplexer_3_out, multiplexer_4_out,
       not_1_out, not_2_out, not_3_out, xnor_1_out, xnor_2_out, xor_1_out, xor_2_out, xor_3_out, xor_4_out,
       xor_5_out;

  and and_1 (Overflow, d_ff_as_1_q, and_2_out);
  xor xor_1 (xor_1_out, d_ff_as_1_q, and_2_out);
  Multiplexer multiplexer_1 (.sel(Enable), .in_0(d_ff_as_1_q), .in_1(xor_1_out), .out(multiplexer_1_out));
  D_FF_AS d_ff_as_1 (.Set(Set), .D(multiplexer_1_out), .C(Clock), .Clr(Clear), .Q(d_ff_as_1_q));  // open: nQ
  and and_2 (and_2_out, d_ff_as_2_q, and_3_out);
  xor xor_2 (xor_2_out, d_ff_as_2_q, and_3_out);
  Multiplexer multiplexer_2 (.sel(Enable), .in_0(d_ff_as_2_q), .in_1(xor_2_out), .out(multiplexer_2_out));
  D_FF_AS d_ff_as_2 (.Set(Set), .D(multiplexer_2_out), .C(Clock), .Clr(Clear), .Q(d_ff_as_2_q));  // open: nQ
  and and_3 (and_3_out, d_ff_as_3_q, and_4_out);
  xor xor_3 (xor_3_out, d_ff_as_3_q, and_4_out);
  Multiplexer multiplexer_3 (.sel(Enable), .in_0(d_ff_as_3_q), .in_1(xor_3_out), .out(multiplexer_3_out));
  not not_1 (not_1_out, d_ff_as_2_q);
  D_FF_AS d_ff_as_3 (.Set(Set), .D(multiplexer_3_out), .C(Clock), .Clr(Clear), .Q(d_ff_as_3_q));  // open: nQ
  not not_2 (not_2_out, d_ff_as_3_q);
  not not_3 (not_3_out, d_ff_as_4_q);
  and and_4 (and_4_out, d_ff_as_4_q, Counter);
  xor xor_4 (xor_4_out, d_ff_as_4_q, Counter);
  Multiplexer multiplexer_4 (.sel(Enable), .in_0(d_ff_as_4_q), .in_1(xor_4_out), .out(multiplexer_4_out));
  xnor xnor_1 (xnor_1_out, d_ff_as_2_q, d_ff_as_4_q);
  xnor xnor_2 (xnor_2_out, d_ff_as_3_q, d_ff_as_4_q);
  and and_5 (and_5_out, d_ff_as_3_q, not_3_out);
  and and_6 (and_6_out, not_1_out, not_3_out);
  and and_7 (and_7_out, not_1_out, d_ff_as_3_q);
  and and_8 (and_8_out, d_ff_as_2_q, not_2_out, d_ff_as_4_q);
  and and_9 (and_9_out, d_ff_as_3_q, not_3_out);
  and and_10 (and_10_out, not_1_out, not_3_out);
  and and_11 (and_11_out, d_ff_as_2_q, not_2_out);
  and and_12 (and_12_out, d_ff_as_2_q, not_3_out);
  and and_13 (and_13_out, not_2_out, not_3_out);
  xor xor_5 (xor_5_out, d_ff_as_2_q, d_ff_as_3_q);
  and and_14 (and_14_out, d_ff_as_3_q, not_3_out);
  D_FF_AS d_ff_as_4 (.Set(Set), .D(multiplexer_4_out), .C(Clock), .Clr(Clear), .Q(d_ff_as_4_q));  // open: nQ
  or or_1 (a, d_ff_as_1_q, d_ff_as_3_q, xnor_1_out);
  or or_2 (b, not_1_out, xnor_2_out);
  or or_3 (c, d_ff_as_2_q, not_2_out, d_ff_as_4_q);
  or or_4 (d, and_5_out, and_6_out, and_7_out, and_8_out);
  or or_5 (e, and_9_out, and_10_out);
  or or_6 (f, d_ff_as_1_q, and_11_out, and_12_out, and_13_out);
  or or_7 (g, d_ff_as_1_q, xor_5_out, and_14_out);
  Seven_Seg seven_seg_1 (.a(a), .b(b), .c(c), .d(d), .e(e), .f(f), .g(g), .dp(1'b0));

  // Notes on the sheet:
  //   2^3
  //   2^2
  //   2^1
  //   2^0
  //   U_3
  //   U_5
  //   U_8
  //   U_9
  //   U_10
  //   U_11
  //   U_13
  //   U_14
  //   U_16
  //   U_17
  //   U_18
  //   U_20
  //   U_21
  //   U_4
  //   U_6
  //   U_7
  //   U_12
  //   U_15
  //   U_19
  //   U_22
endmodule
