// Digital circuit D_Flip_Flop_SetClear.dig as structural Verilog
module D_Flip_Flop_SetClear (
  input  D,
  input  Clock,
  input  Set,
  input  Clear,
  output Q
);

  wire nand_1_out, nand_2_out, nand_3_out, nand_4_out, nand_5_out, nand_6_out, nand_8_out, not_1_out,
       not_2_out, not_3_out, not_4_out, not_5_out;

  not not_1 (not_1_out, Clock);
  not not_2 (not_2_out, D);
  nand nand_1 (nand_1_out, D, not_1_out);
  nand nand_2 (nand_2_out, not_1_out, not_2_out);
  not not_3 (not_3_out, Set);
  not not_4 (not_4_out, Clear);
  nand nand_3 (nand_3_out, not_3_out, nand_1_out, nand_4_out);
  nand nand_4 (nand_4_out, nand_3_out, nand_2_out, not_4_out);
  not not_5 (not_5_out, nand_3_out);
  nand nand_5 (nand_5_out, nand_3_out, Clock);
  nand nand_6 (nand_6_out, Clock, not_5_out);
  nand nand_7 (Q, not_3_out, nand_5_out, nand_8_out);
  nand nand_8 (nand_8_out, Q, nand_6_out, not_4_out);
endmodule
