// Digital circuit D_Latch.dig as structural Verilog
module D_Latch (
  input  D,
  output Q,
  output Q_2
);

  wire not_1_out;

  not not_1 (not_1_out, D);
  nand nand_1 (Q, not_1_out, Q_2);
  nand nand_2 (Q_2, Q, D);
endmodule
