// Digital circuit SR_Latch_w_Enable.dig as structural Verilog
module SR_Latch_w_Enable (
  input  S,
  input  R,
  input  Enable,
  output Q,
  output Q_2
);

  wire nand_1_out, nand_2_out;

  nand nand_1 (nand_1_out, S, Enable);
  nand nand_2 (nand_2_out, Enable, R);
  nand nand_3 (Q, nand_1_out, Q_2);
  nand nand_4 (Q_2, Q, nand_2_out);
endmodule
