// Digital circuit Shift_Register.dig as structural Verilog
module Shift_Register (
  input  Enable,
  input  Clock,
  input  Clear,
  input  Set,
  input  D3,
  output out_6,
  output out_7,
  output out_8,
  output out_9
);

  wire multiplexer_1_out, multiplexer_2_out, multiplexer_3_out, multiplexer_4_out;

  Multiplexer multiplexer_1 (.sel(Enable), .in_0(out_6), .in_1(D3), .out(multiplexer_1_out));
  D_FF_AS d_ff_as_1 (.Set(Set), .D(multiplexer_1_out), .C(Clock), .Clr(Clear), .Q(out_6));  // open: nQ
  Multiplexer multiplexer_2 (.sel(Enable), .in_0(out_7), .in_1(out_6), .out(multiplexer_2_out));
  D_FF_AS d_ff_as_2 (.Set(Set), .D(multiplexer_2_out), .C(Clock), .Clr(Clear), .Q(out_7));  // open: nQ
  Multiplexer multiplexer_3 (.sel(Enable), .in_0(out_8), .in_1(out_7), .out(multiplexer_3_out));
  D_FF_AS d_ff_as_3 (.Set(Set), .D(multiplexer_3_out), .C(Clock), .Clr(Clear), .Q(out_8));  // open: nQ
  Multiplexer multiplexer_4 (.sel(Enable), .in_0(out_9), .in_1(out_8), .out(multiplexer_4_out));
  D_FF_AS d_ff_as_4 (.Set(Set), .D(multiplexer_4_out), .C(Clock), .Clr(Clear), .Q(out_9));  // open: nQ
endmodule
