// Digital circuit 3_Input_NAND_optim.dig as structural Verilog
module _3_Input_NAND_optim (
  input  A,
  input  B,
  input  C,
  output Output
);

  wire fgpfet_1_d, fgpfet_2_d;

  FGNFET fgnfet_1 (.G(A), .D(1'b1), .S(Output));
  FGNFET fgnfet_2 (.G(B), .D(1'b1), .S(Output));
  FGNFET fgnfet_3 (.G(C), .D(1'b1), .S(Output));
  FGPFET fgpfet_1 (.G(C), .S(Output), .D(fgpfet_1_d));
  FGPFET fgpfet_2 (.G(B), .S(fgpfet_1_d), .D(fgpfet_2_d));
  FGPFET fgpfet_3 (.G(A), .S(fgpfet_2_d), .D(1'b0));
endmodule
