// Digital circuit AdderSubs_4bit.dig as structural Verilog
module AdderSubs_4bit (
  input  Y_i0,
  input  X_i0,
  input  Y_i1,
  input  X_i1,
  input  Y_i2,
  input  X_i2,
  input  Y_i3,
  input  X_i3,
  input  Sel,
  output S_i0,
  output S_i1,
  output S_i2,
  output S_i3,
  output out_14,
  output out_15
);

  wire and_1_out, and_2_out, and_3_out, and_4_out, and_5_out, and_6_out, and_7_out, and_8_out, or_2_out,
       or_3_out, or_4_out, xor_2_out, xor_3_out, xor_5_out, xor_6_out, xor_8_out, xor_9_out, xor_11_out,
       xor_12_out;

  xor xor_1 (out_15, and_2_out, out_14);
  or or_1 (out_14, and_2_out, and_1_out);
  and and_1 (and_1_out, xor_2_out, X_i3);
  and and_2 (and_2_out, or_2_out, xor_3_out);
  xor xor_2 (xor_2_out, Y_i3, Sel);
  xor xor_3 (xor_3_out, xor_2_out, X_i3);
  xor xor_4 (S_i3, or_2_out, xor_3_out);
  or or_2 (or_2_out, and_4_out, and_3_out);
  and and_3 (and_3_out, xor_5_out, X_i2);
  and and_4 (and_4_out, or_3_out, xor_6_out);
  xor xor_5 (xor_5_out, Y_i2, Sel);
  xor xor_6 (xor_6_out, xor_5_out, X_i2);
  xor xor_7 (S_i2, or_3_out, xor_6_out);
  or or_3 (or_3_out, and_6_out, and_5_out);
  and and_5 (and_5_out, xor_8_out, X_i1);
  and and_6 (and_6_out, or_4_out, xor_9_out);
  xor xor_8 (xor_8_out, Y_i1, Sel);
  xor xor_9 (xor_9_out, xor_8_out, X_i1);
  xor xor_10 (S_i1, or_4_out, xor_9_out);
  or or_4 (or_4_out, and_8_out, and_7_out);
  and and_7 (and_7_out, xor_11_out, X_i0);
  and and_8 (and_8_out, Sel, xor_12_out);
  xor xor_11 (xor_11_out, Y_i0, Sel);
  xor xor_12 (xor_12_out, xor_11_out, X_i0);
  xor xor_13 (S_i0, Sel, xor_12_out);

  // Notes on the sheet:
  //   FA_i
  //   X_in = a
  //   Y_in = b
  //   a+b o a-b
endmodule
