// Digital circuit BDC_7_Segments.dig as structural Verilog
module BDC_7_Segments (
  input  i_0,
  input  i_1,
  input  i_2,
  input  i_3
);

  wire a, and_1_out, and_2_out, and_3_out, and_4_out, and_5_out, and_6_out, and_7_out, and_8_out, and_9_out,
       and_10_out, b, c, d, e, f, g, not_1_out, not_2_out, not_3_out, xnor_1_out, xnor_2_out, xor_1_out;

  not not_1 (not_1_out, i_2);
  not not_2 (not_2_out, i_1);
  not not_3 (not_3_out, i_0);
  xnor xnor_1 (xnor_1_out, i_2, i_0);
  xnor xnor_2 (xnor_2_out, i_1, i_0);
  and and_1 (and_1_out, i_1, not_3_out);
  and and_2 (and_2_out, not_1_out, not_3_out);
  and and_3 (and_3_out, not_1_out, i_1);
  and and_4 (and_4_out, i_2, not_2_out, i_0);
  and and_5 (and_5_out, i_1, not_3_out);
  and and_6 (and_6_out, not_1_out, not_3_out);
  and and_7 (and_7_out, i_2, not_2_out);
  and and_8 (and_8_out, i_2, not_3_out);
  and and_9 (and_9_out, not_2_out, not_3_out);
  xor xor_1 (xor_1_out, i_2, i_1);
  and and_10 (and_10_out, i_1, not_3_out);
  or or_1 (a, i_3, i_1, xnor_1_out);
  or or_2 (b, not_1_out, xnor_2_out);
  or or_3 (c, i_2, not_2_out, i_0);
  or or_4 (d, and_1_out, and_2_out, and_3_out, and_4_out);
  or or_5 (e, and_5_out, and_6_out);
  or or_6 (f, i_3, and_7_out, and_8_out, and_9_out);
  or or_7 (g, i_3, xor_1_out, and_10_out);
  Seven_Seg seven_seg_1 (.a(a), .b(b), .c(c), .d(d), .e(e), .f(f), .g(g), .dp(1'b0));

  // Notes on the sheet:
  //   2^3
  //   2^2
  //   2^1
  //   2^0
  //   U_3
  //   U_5
  //   U_8
  //   U_9
  //   U_10
  //   U_11
  //   U_13
  //   U_14
  //   U_16
  //   U_17
  //   U_18
  //   U_20
  //   U_21
  //   U_4
  //   U_6
  //   U_7
  //   U_12
  //   U_15
  //   U_19
  //   U_22
endmodule
