// Digital circuit Ejercicio_3.dig as structural Verilog
module Ejercicio_3 (
  input  x,
  input  y,
  input  z,
  output f
);

  wire and_1_out, and_2_out, and_3_out, and_4_out, not_1_out, not_2_out;

  not not_1 (not_1_out, x);
  not not_2 (not_2_out, y);
  and and_1 (and_1_out, not_1_out, not_2_out, z);
  and and_2 (and_2_out, not_1_out, y, z);
  and and_3 (and_3_out, x, not_2_out, z);
  and and_4 (and_4_out, x, y);
  or or_1 (f, and_1_out, and_2_out, and_3_out, and_4_out);

  // Notes on the sheet:
  //   x¬
  //   y¬
  //   y
  //   x
  //   z
  //   x¬y¬z
  //   x¬yz
  //   xy¬z
  //   xy
endmodule
