// Digital circuit Or_Madeof_NAND.dig as structural Verilog
module Or_Madeof_NAND (
  input  A,
  input  B,
  output Output
);

  wire nfet_1_s, nfet_3_s, nfet_5_s, Output_A, Output_B;

  PFET pfet_1 (.G(A), .S(1'b1), .D(Output_A));
  NFET nfet_1 (.G(A), .D(Output_A), .S(nfet_1_s));
  NFET nfet_2 (.G(A), .D(nfet_1_s), .S(1'b0));
  PFET pfet_2 (.G(A), .S(1'b1), .D(Output_A));
  PFET pfet_3 (.G(B), .S(1'b1), .D(Output_B));
  NFET nfet_3 (.G(B), .D(Output_B), .S(nfet_3_s));
  NFET nfet_4 (.G(B), .D(nfet_3_s), .S(1'b0));
  PFET pfet_4 (.G(B), .S(1'b1), .D(Output_B));
  PFET pfet_5 (.G(Output_A), .S(1'b1), .D(Output));
  NFET nfet_5 (.G(Output_B), .D(Output), .S(nfet_5_s));
  NFET nfet_6 (.G(Output_A), .D(nfet_5_s), .S(1'b0));
  PFET pfet_6 (.G(Output_B), .S(1'b1), .D(Output));

  // Other names for the same wires on the sheet: Input_A = A; Input_B = B
endmodule
